# Fritzing sketch MindFlora (saved by Fritzing 1.0.4)
breadboards: 1

parts:
  MCU1 = Raspberry Pi Zero
  ADC1 = MCP3008 [package=dil16]
  RHT1 = Humidity and Temperature Sensor RHT03
  부품1 = Soil Moisture Sensor
  Power_plug1 = Power plug  # not connected
  M2 = CK-07 [package=THT]
  M1 = DC Motor [voltage_(max)=6V voltage_(min)=3V]
  Mod1 = KY-019 5V Relay Module [package="Breakout board"]
  L298N2 = L298N DC motor driver
  U1 = WS2812 RGB LED strip
  부품2 = I2C level shifter bidirectional  # not connected

nets:
  VCC: MCU1.pin_1, MCU1.pin_17, ADC1.VREF, ADC1.VDD, RHT1.Vcc, 부품1.VCC, M2.pin_4, Mod1.+
  GND: MCU1.pin_9, MCU1.pin_14, MCU1.pin_34, ADC1.DGND, ADC1.AGND, RHT1.GND_1, 부품1.GND, M2.pin_3, M1.pin_2, Mod1.-, L298N2.GND
  N1: MCU1.pin_19, ADC1.CLK
  N2: MCU1.pin_21, ADC1.Dout
  N3: MCU1.pin_23, ADC1.Din
  N4: MCU1.pin_24, ADC1.CS/SHDN
  N5: MCU1.pin_37, Mod1.S
  N6: ADC1.CH4, RHT1.Data-signal
  N7: ADC1.CH5, 부품1.SIG
  N8: ADC1.CH7, M2.pin_1
  N9: M1.pin_1, Mod1.NC
  N10: Mod1.Common, L298N2.5V
  N11: L298N2.OUT3, U1.VCC
  N12: L298N2.OUT4, U1.GND

notes:
  광센서
  DHT11 온습도센서
  부품 목록
  DHT11 (가)
  MCP3208 (부)
  CDS Module (가)
  Soil Moisture (가)
  Relay 2개 (부)
  토양습도센서
  Pump = DC Motor
  극성주의
  물 방향 보고 결정
  DC 5V
  3A input
  도합 예측 전력소모량
  PiZero 300mA
  DC 모터 (가동시 300mA)
  센서 도합 10mA
  전선을 잘라서
  분산투입

custom parts:
  CK-07: Fc-51 Infrared Obstacle Avoidance Proximity Sensor module. IR transmitter led, receiver LED, lm393 compaitor and a pot. 3.3 V to 5V power.
  KY-019 5V Relay Module: KY-019 5V Relay module, used to control AC circuits. (Special thanks to vanepp for fixing the PCB holes and other errors)
  L298N DC motor driver: 2x DC motor driver with 78M05 positive voltage regulator (7..35 V) L298N: max 46 V, 2 A Set 5 V Enable jumper to enable 5 V regultor (needed for the L298N) and +5 V output at screw terminal or supply external +5 V at screw terminal Set ENA and/or ENB to +5 V to enable motor permanently or supply ENA and/or ENB with PWM signal IN1 and IN2 set rotation directory for motor A (OUT1/OUT2) IN2 and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
  WS2812 RGB LED strip: WS2812 strip
